# Fritzing sketch Smart heaven (saved by Fritzing 0.9.3b)

parts:
  U1 = 4-Channel 5v Relay Shield [package=relay-4ch5v10a]
  Part1 = Bluetooth HC-05 Macho
  IR2 = TSOP312.., 314.. [package=THT]
  U2 = LuaNode32 / ESP32
  S1 = Pushbutton [package="[THT]"]
  S2 = Pushbutton [package="[THT]"]
  S3 = Pushbutton [package="[THT]"]
  S4 = Pushbutton [package="[THT]"]
  BULB1 = Incandescent light bulb small [package="bulb sm"]
  BULB2 = Incandescent light bulb small [package="bulb sm"]
  BULB3 = Incandescent light bulb small [package="bulb sm"]
  BULB4 = Incandescent light bulb small [package="bulb sm"]
  J1 = 220v plug
  JACK1 = 2.1mm Barrel Jack with Terminal Block

nets:
  VCC: U1.VCC, Part1.VCC, IR2.Vs, JACK1.POS
  N1: U1.GND, S4.Pin_1, S4.Pin_2
  N2: U1.IN1, U2.D23
  N3: U1.IN2, U2.D22
  N4: U1.K1-Off, J1.pin1
  N5: U1.K1-On, BULB1.2
  N6: U1.K2-On, BULB2.2
  N7: U1.IN4, U2.D19
  N8: U1.K3-On, BULB3.2
  N9: U1.K4-On, BULB4.2
  N10: U1.IN3, U2.D21
  N11: Part1.TXD, U2.RX2
  GND: Part1.GND, IR2.GND, U2.GND
  N12: IR2.Data, U2.D35
  N13: U2.D27, S1.Pin_3, S1.Pin_4
  N14: U2.D14, S2.Pin_3, S2.Pin_4
  N15: U2.D12, S3.Pin_3, S3.Pin_4
  N16: U2.D13, S4.Pin_3, S4.Pin_4
  N17: BULB1.1, J1.pin2

custom parts:
  4-Channel 5v Relay Shield: 4 Channel 5v Relay Shield w. 2x SPD-06VDC-SD-C
  LuaNode32 / ESP32: ESP32 based LuaNode32
  220v plug: Generic 220V AC plug.
